// Logisim project FULLADDER8.circ as structural Verilog: 2 circuits, main circuit fulladder
module fulladder (
  input  in_1,
  input  in_2,
  input  CIN,
  output SUM,
  output Cout
);

  wire and_1_out, and_2_out, xor_1_out;

  xor xor_1 (xor_1_out, in_1, in_2);
  xor xor_2 (SUM, xor_1_out, CIN);
  and and_1 (and_1_out, xor_1_out, CIN);
  and and_2 (and_2_out, in_1, in_2);
  or or_1 (Cout, and_1_out, and_2_out);
endmodule

module fulladder8 (
  input  CIN,
  input  [7:0] X,
  input  [7:0] Y,
  output [7:0] SUM,
  output COUT
);

  wire fulladder_1_cout, fulladder_2_cout, fulladder_3_cout, fulladder_4_cout, fulladder_5_cout,
       fulladder_6_cout, fulladder_7_cout;

  fulladder fulladder_1 (.in_1(X[0]), .in_2(Y[0]), .CIN(CIN), .SUM(SUM[0]), .Cout(fulladder_1_cout));
  fulladder fulladder_2 (.in_1(X[1]), .in_2(Y[1]), .CIN(fulladder_1_cout), .SUM(SUM[1]), .Cout(fulladder_2_cout));
  fulladder fulladder_3 (.in_1(X[2]), .in_2(Y[2]), .CIN(fulladder_2_cout), .SUM(SUM[2]), .Cout(fulladder_3_cout));
  fulladder fulladder_4 (.in_1(X[3]), .in_2(Y[3]), .CIN(fulladder_3_cout), .SUM(SUM[3]), .Cout(fulladder_4_cout));
  fulladder fulladder_5 (.in_1(X[4]), .in_2(Y[4]), .CIN(fulladder_4_cout), .SUM(SUM[4]), .Cout(fulladder_5_cout));
  fulladder fulladder_6 (.in_1(X[5]), .in_2(Y[5]), .CIN(fulladder_5_cout), .SUM(SUM[5]), .Cout(fulladder_6_cout));
  fulladder fulladder_7 (.in_1(X[6]), .in_2(Y[6]), .CIN(fulladder_6_cout), .SUM(SUM[6]), .Cout(fulladder_7_cout));
  fulladder fulladder_8 (.in_1(X[7]), .in_2(Y[7]), .CIN(fulladder_7_cout), .SUM(SUM[7]), .Cout(COUT));
endmodule
