// Logisim project customComparator.circ as structural Verilog: 1 circuit, main circuit main
module main (
  input  [7:0] X,
  input  [7:0] Y,
  output EQUAL
);

  wire xnor_1_out, xnor_2_out, xnor_3_out, xnor_4_out, xnor_5_out, xnor_6_out, xnor_7_out, xnor_8_out;

  xnor xnor_1 (xnor_1_out, X[0], Y[0]);
  xnor xnor_2 (xnor_2_out, X[1], Y[1]);
  xnor xnor_3 (xnor_3_out, X[2], Y[2]);
  xnor xnor_4 (xnor_4_out, X[3], Y[3]);
  xnor xnor_5 (xnor_5_out, X[4], Y[4]);
  xnor xnor_6 (xnor_6_out, Y[5], X[5]);
  xnor xnor_7 (xnor_7_out, X[6], Y[6]);
  xnor xnor_8 (xnor_8_out, X[7], Y[7]);
  and and_1 (EQUAL, xnor_1_out, xnor_2_out, xnor_3_out, xnor_4_out, xnor_5_out, xnor_6_out, xnor_7_out, xnor_8_out);
endmodule
