// Logisim project rotr.circ as structural Verilog: 1 circuit, main circuit main
module main (
  input  [7:0] X,
  input  [2:0] Y,
  output [7:0] RESULT
);

  Multiplexer #(.select(3)) multiplexer_1 (
    .in0(X[7]), .in1(X[0]), .in2(X[1]), .in3(X[2]), .in4(X[3]), .in5(X[4]), .in6(X[5]), .in7(X[6]),
    .out(RESULT[7]), .sel(Y));
  Multiplexer #(.select(3)) multiplexer_2 (
    .in0(X[6]), .in1(X[7]), .in2(X[0]), .in3(X[1]), .in4(X[2]), .in5(X[3]), .in6(X[4]), .in7(X[5]),
    .out(RESULT[6]), .sel(Y));
  Multiplexer #(.select(3)) multiplexer_3 (
    .in0(X[5]), .in1(X[6]), .in2(X[7]), .in3(X[0]), .in4(X[1]), .in5(X[2]), .in6(X[3]), .in7(X[4]),
    .out(RESULT[5]), .sel(Y));
  Multiplexer #(.select(3)) multiplexer_4 (
    .in0(X[4]), .in1(X[5]), .in2(X[6]), .in3(X[7]), .in4(X[0]), .in5(X[1]), .in6(X[2]), .in7(X[3]),
    .out(RESULT[4]), .sel(Y));
  Multiplexer #(.select(3)) multiplexer_5 (
    .in0(X[3]), .in1(X[4]), .in2(X[5]), .in3(X[6]), .in4(X[7]), .in5(X[0]), .in6(X[1]), .in7(X[2]),
    .out(RESULT[3]), .sel(Y));
  Multiplexer #(.select(3)) multiplexer_6 (
    .in0(X[2]), .in1(X[3]), .in2(X[4]), .in3(X[5]), .in4(X[6]), .in5(X[7]), .in6(X[0]), .in7(X[1]),
    .out(RESULT[2]), .sel(Y));
  Multiplexer #(.select(3)) multiplexer_7 (
    .in0(X[1]), .in1(X[2]), .in2(X[3]), .in3(X[4]), .in4(X[5]), .in5(X[6]), .in6(X[7]), .in7(X[0]),
    .out(RESULT[1]), .sel(Y));
  Multiplexer #(.select(3)) multiplexer_8 (
    .in0(X[0]), .in1(X[1]), .in2(X[2]), .in3(X[3]), .in4(X[4]), .in5(X[5]), .in6(X[6]), .in7(X[7]),
    .out(RESULT[0]), .sel(Y));
endmodule
