// Logisim project twosComplement.circ as structural Verilog: 1 circuit, main circuit main
module main (
  input  [7:0] X,
  output [7:0] COMPL
);

  wire [7:0] not_1_out;

  assign not_1_out = ~X;  // NOT_Gate not_1, 8 bits wide
  Adder adder_1 (.a(not_1_out), .b(8'h1), .out(COMPL));  // open: cin, cout
endmodule
