// Logisim project cng331projepart2.circ as structural Verilog: 7 circuits, main circuit ALU8
// ALU
module ALU8 (
  input  [7:0] X,
  input  [7:0] Y,
  input  [1:0] ALUfunc,
  output [7:0] RESULT
);

  wire [7:0] adder_1_out, and_1_out, or_1_out, shifter_1_out;

  Adder adder_1 (.a(X), .b(Y), .out(adder_1_out));  // open: cin, cout
  Shifter #(.shift("rl")) shifter_1 (.in(X), .\dist (Y[2:0]), .out(shifter_1_out));
  assign and_1_out = X & Y;  // AND_Gate and_1, 8 bits wide
  assign or_1_out = X | Y;  // OR_Gate or_1, 8 bits wide
  Multiplexer #(.select(2), .width(8)) multiplexer_1 (
    .in0(adder_1_out), .in1(and_1_out), .in2(or_1_out), .in3(shifter_1_out), .out(RESULT), .sel(ALUfunc));
endmodule

module ROMcurcit (
  input  [9:0] in_1,
  output [20:0] out_2
);

  ROM #(.addrWidth(10), .dataWidth(21), .misaligned("true")) rom_1 (.addr(in_1), .data(out_2));

  // Notes on the sheet:
  //   contents of rom_1 (hex, n*v repeats v):
  //   0 60503 60702 17e00 197c00 43002 93224 20302 10e600 19100 40805
endmodule

module Ramcurcit (
  input  [7:0] Address,
  input  write,
  input  read,
  input  clock,
  input  [7:0] data,
  output [7:0] out_6
);

  RAM #(.asyncread("true"), .trigger("falling")) ram_1 (
    .addr(Address), .we(write), .oe(read), .clk(clock), .din(data), .dout(out_6));
endmodule

module maincircuit (
  input  [9:0] in_1,
  input  in_2,
  output [9:0] out_3,
  output [7:0] out_4,
  output [2:0] out_5
);

  wire clock_1_out, controlunit_1_mux2, controlunit_1_mw, controlunit_1_we, controlunit_1_wr;
  wire [1:0] controlunit_1_alufunc0, controlunit_1_mux10;
  wire [7:0] alu8_1_result, main_1_out_7, main_1_out_8, multiplexer_2_out, ramcurcit_1_out_6;
  wire [20:0] romcurcit_1_out_2;
  wire [23:0] bit_extender_1_out;

  Clock clock_1 (.out(clock_1_out));
  pc pc_1 (.data(in_1), .clock(clock_1_out), .reset(in_2), .out_4(out_3));
  assign {bit_extender_1_out[23:11], out_5, bit_extender_1_out[7:0]} = {{3{romcurcit_1_out_2[20]}}, romcurcit_1_out_2};  // Bit_Extender bit_extender_1
  ROMcurcit romcurcit_1 (.in_1(out_3), .out_2(romcurcit_1_out_2));
  Multiplexer #(.select(2), .width(8)) multiplexer_1 (
    .in0(alu8_1_result), .in1(ramcurcit_1_out_6), .in2(bit_extender_1_out[7:0]), .out(out_4),
    .sel(controlunit_1_mux10));  // open: in3
  ControlUnit controlunit_1 (
    .opcode0(bit_extender_1_out[17]), .opcode1(bit_extender_1_out[18]), .opcode2(bit_extender_1_out[19]),
    .opcode3(bit_extender_1_out[20]), .mux10(controlunit_1_mux10[0]), .mux11(controlunit_1_mux10[1]),
    .mux2(controlunit_1_mux2), .WE(controlunit_1_we), .MW(controlunit_1_mw), .WR(controlunit_1_wr),
    .Alufunc0(controlunit_1_alufunc0[0]), .Alufunc1(controlunit_1_alufunc0[1]));
  Multiplexer #(.width(8)) multiplexer_2 (
    .in0(main_1_out_7), .in1(bit_extender_1_out[7:0]), .out(multiplexer_2_out), .sel(controlunit_1_mux2));
  main main_1 (
    .WE(controlunit_1_we), .rd(out_5), .data(out_4), .clock(clock_1_out), .rt(bit_extender_1_out[13:11]),
    .rs(bit_extender_1_out[16:14]), .out_7(main_1_out_7), .out_8(main_1_out_8));
  ALU8 alu8_1 (.X(main_1_out_8), .Y(multiplexer_2_out), .ALUfunc(controlunit_1_alufunc0), .RESULT(alu8_1_result));
  Ramcurcit ramcurcit_1 (
    .Address(alu8_1_result), .write(controlunit_1_mw), .read(controlunit_1_wr), .clock(clock_1_out),
    .data(main_1_out_7), .out_6(ramcurcit_1_out_6));

  // Other names for the same wires on the sheet: A[7:0] = out_4
endmodule

module main (
  input  WE,
  input  [2:0] rd,
  input  [7:0] data,
  input  clock,
  input  [2:0] rt,
  input  [2:0] rs,
  output [7:0] out_7,
  output [7:0] out_8
);

  wire decoder_1_out0, decoder_1_out1, decoder_1_out2, decoder_1_out3, decoder_1_out4, decoder_1_out5,
       decoder_1_out6, decoder_1_out7;
  wire [7:0] register_1_q, register_2_q, register_3_q, register_4_q, register_5_q, register_6_q,
       register_7_q, register_8_q;

  Multiplexer #(.select(3), .width(8)) multiplexer_1 (
    .in0(register_1_q), .in1(register_2_q), .in2(register_3_q), .in3(register_4_q), .in4(register_5_q),
    .in5(register_6_q), .in6(register_7_q), .in7(register_8_q), .out(out_7), .sel(rt));
  Multiplexer #(.select(3), .width(8)) multiplexer_2 (
    .in0(register_1_q), .in1(register_2_q), .in2(register_3_q), .in3(register_4_q), .in4(register_5_q),
    .in5(register_6_q), .in6(register_7_q), .in7(register_8_q), .out(out_8), .sel(rs));
  Decoder #(.select(3)) decoder_1 (
    .out0(decoder_1_out0), .out1(decoder_1_out1), .out2(decoder_1_out2), .out3(decoder_1_out3),
    .out4(decoder_1_out4), .out5(decoder_1_out5), .out6(decoder_1_out6), .out7(decoder_1_out7), .sel(rd),
    .en(WE));
  Register #(.trigger("falling")) register_1 (
    .D(data), .en(decoder_1_out0), .clk(clock), .Q(register_1_q));  // open: clr
  Register #(.trigger("falling")) register_2 (
    .D(data), .en(decoder_1_out1), .clk(clock), .Q(register_2_q));  // open: clr
  Register #(.trigger("falling")) register_3 (
    .D(data), .en(decoder_1_out2), .clk(clock), .Q(register_3_q));  // open: clr
  Register #(.trigger("falling")) register_4 (
    .D(data), .en(decoder_1_out3), .clk(clock), .Q(register_4_q));  // open: clr
  Register #(.trigger("falling")) register_5 (
    .D(data), .en(decoder_1_out4), .clk(clock), .Q(register_5_q));  // open: clr
  Register #(.trigger("falling")) register_6 (
    .D(data), .en(decoder_1_out5), .clk(clock), .Q(register_6_q));  // open: clr
  Register #(.trigger("falling")) register_7 (
    .D(data), .en(decoder_1_out6), .clk(clock), .Q(register_7_q));  // open: clr
  Register #(.trigger("falling")) register_8 (
    .D(data), .en(decoder_1_out7), .clk(clock), .Q(register_8_q));  // open: clr
endmodule

module ControlUnit (
  input  opcode0,
  input  opcode1,
  input  opcode2,
  input  opcode3,
  output mux10,
  output mux11,
  output mux2,
  output WE,
  output MW,
  output WR,
  output Alufunc0,
  output Alufunc1
);

  wire not_1_out, not_2_out, not_3_out, not_4_out;

  not not_1 (not_1_out, opcode1);
  and and_1 (mux10, opcode0, not_1_out);
  not not_2 (not_2_out, opcode1);
  not not_3 (not_3_out, opcode0);
  not not_4 (not_4_out, opcode1);
  and and_2 (mux11, opcode0, opcode1);
  or or_1 (mux2, opcode0, opcode1);
  or or_2 (WE, opcode0, not_2_out);
  and and_3 (MW, not_3_out, opcode1);
  and and_4 (WR, opcode0, not_4_out);

  assign Alufunc0 = opcode2;
  assign Alufunc1 = opcode3;

  // Other names for the same wires on the sheet: A = opcode0; B = opcode1; C = opcode2; D = opcode3
endmodule

module pc (
  input  [9:0] data,
  input  clock,
  input  reset,
  output [9:0] out_4
);

  Counter #(.max('h3ff), .width(10)) counter_1 (
    .load(1'b0), .D(data), .count(1'b1), .Q(out_4), .up(1'b1), .clk(clock), .clr(reset));  // open: carry
endmodule
